// Logisim project minirv.circ as structural Verilog: 7 circuits, main circuit main
module main (
  input  EN,
  input  Rst,
  output [15:0] out_3
);

  wire and_12_out, and_15_out, and_16_out, clock_1_out, comparator_1_eq, comparator_2_eq, comparator_3_eq,
       comparator_4_eq, comparator_5_eq, comparator_6_eq, comparator_7_eq, comparator_8_eq, comparator_9_eq,
       comparator_10_eq, comparator_11_eq, comparator_12_eq, comparator_13_eq, not_1_out, or_1_out, or_3_out,
       or_9_out;
  wire [0:0] adder_2_out;
  wire [3:0] and_22_out, decoder_1_out3, or_8_out;
  wire [7:0] multiplexer_1_out;
  wire [23:0] or_7_out, pc_register_32_bit_1_out3;
  wire [31:0] adder_1_out, adder_3_out, adder_4_out, and_1_out, and_2_out, and_9_out, and_13_out, and_14_out,
       and_17_out, and_18_out, and_19_out, and_20_out, and_21_out, bit_extender_1_out, bit_extender_2_out,
       bit_extender_3_out, gpr_ram_32_32bit_1_read1, gpr_ram_32_32bit_1_read2, or_2_out, or_4_out, or_5_out,
       or_6_out, pc_register_32_bit_1_out_32_bit, ram_1_dout, rom_1_data;
  wire [31:1] adder_2_out_2;
  wire [31:31] and_3_out, and_4_out, and_5_out, and_6_out, and_7_out, and_8_out, and_10_out, and_11_out;

  Clock clock_1 (.out(clock_1_out));
  // Probe on out_3
  Sixteen_bit_counter sixteen_bit_counter_1 (.EN(EN), .clk(clock_1_out), .Rst(Rst), .out_4(out_3));
  PC_Register_32_bit pc_register_32_bit_1 (
    .addr({adder_2_out_2, 1'b0}), .flag(or_1_out), .EN(EN), .clk(clock_1_out), .Rst(Rst),
    .Out3(pc_register_32_bit_1_out3[0]), .Out4(pc_register_32_bit_1_out3[1]),
    .out_10(pc_register_32_bit_1_out3[2]), .out_11(pc_register_32_bit_1_out3[3]),
    .out_12(pc_register_32_bit_1_out3[4]), .out_13(pc_register_32_bit_1_out3[5]),
    .out_14(pc_register_32_bit_1_out3[6]), .out_15(pc_register_32_bit_1_out3[7]),
    .out_16(pc_register_32_bit_1_out3[8]), .out_17(pc_register_32_bit_1_out3[9]),
    .out_18(pc_register_32_bit_1_out3[10]), .out_19(pc_register_32_bit_1_out3[11]),
    .out_20(pc_register_32_bit_1_out3[12]), .out_21(pc_register_32_bit_1_out3[13]),
    .out_22(pc_register_32_bit_1_out3[14]), .out_23(pc_register_32_bit_1_out3[15]),
    .out_24(pc_register_32_bit_1_out3[16]), .out_25(pc_register_32_bit_1_out3[17]),
    .out_26(pc_register_32_bit_1_out3[18]), .out_27(pc_register_32_bit_1_out3[19]),
    .out_28(pc_register_32_bit_1_out3[20]), .out_29(pc_register_32_bit_1_out3[21]),
    .out_30(pc_register_32_bit_1_out3[22]), .out_31(pc_register_32_bit_1_out3[23]),
    .Out_32_bit(pc_register_32_bit_1_out_32_bit));  // open: Out1, Out2, out_32, out_33, Out28, Out29, Out30, Out31
  ROM #(.addrWidth(24), .dataWidth(32)) rom_1 (.addr(pc_register_32_bit_1_out3), .data(rom_1_data));
  Adder #(.width(32)) adder_1 (.a(32'h4), .b(pc_register_32_bit_1_out_32_bit), .out(adder_1_out));  // open: cin, cout
  assign and_1_out = {32{and_3_out[31]}} & adder_1_out;  // AND_Gate and_1, 32 bits wide
  assign bit_extender_1_out = {{20{rom_1_data[31]}}, rom_1_data[31:20]};  // Bit_Extender bit_extender_1
  or or_1 (or_1_out, and_8_out[31], not_1_out);
  assign and_2_out = {rom_1_data[31:12], {12{1'b0}}} & {32{and_11_out[31]}};  // AND_Gate and_2, 32 bits wide
  Comparator #(.mode("unsigned"), .width(7)) comparator_1 (
    .a(rom_1_data[6:0]), .b(7'b0100011), .eq(comparator_1_eq));  // open: gt, lt
  Comparator #(.mode("unsigned"), .width(3)) comparator_2 (
    .a(rom_1_data[14:12]), .b(3'b000), .eq(comparator_2_eq));  // open: gt, lt
  not not_1 (not_1_out, and_3_out[31]);
  Comparator #(.mode("unsigned"), .width(7)) comparator_3 (
    .a(rom_1_data[6:0]), .b(7'b1100111), .eq(comparator_3_eq));  // open: gt, lt
  Comparator #(.mode("unsigned"), .width(7)) comparator_4 (
    .a(rom_1_data[6:0]), .b(7'b0010011), .eq(comparator_4_eq));  // open: gt, lt
  Comparator #(.mode("unsigned"), .width(3)) comparator_5 (
    .a(rom_1_data[14:12]), .b(3'b000), .eq(comparator_5_eq));  // open: gt, lt
  Comparator #(.mode("unsigned"), .width(7)) comparator_6 (
    .a(7'b0110011), .b(rom_1_data[6:0]), .eq(comparator_6_eq));  // open: gt, lt
  assign or_2_out = and_1_out | and_2_out | and_9_out | and_17_out | and_13_out | and_14_out;  // OR_Gate or_2, 32 bits wide
  Comparator #(.mode("unsigned"), .width(7)) comparator_7 (
    .a(rom_1_data[6:0]), .b(7'b0000011), .eq(comparator_7_eq));  // open: gt, lt
  Comparator #(.mode("unsigned"), .width(3)) comparator_8 (
    .a(rom_1_data[14:12]), .b(3'b100), .eq(comparator_8_eq));  // open: gt, lt
  Comparator #(.mode("unsigned"), .width(7)) comparator_9 (
    .a(rom_1_data[6:0]), .b(7'b0100011), .eq(comparator_9_eq));  // open: gt, lt
  Comparator #(.mode("unsigned"), .width(3)) comparator_10 (
    .a(rom_1_data[14:12]), .b(3'b010), .eq(comparator_10_eq));  // open: gt, lt
  Comparator #(.mode("unsigned"), .width(7)) comparator_11 (
    .a(rom_1_data[6:0]), .b(7'b0000011), .eq(comparator_11_eq));  // open: gt, lt
  Comparator #(.mode("unsigned"), .width(3)) comparator_12 (
    .a(rom_1_data[14:12]), .b(3'b010), .eq(comparator_12_eq));  // open: gt, lt
  Comparator #(.mode("unsigned"), .width(7)) comparator_13 (
    .a(rom_1_data[6:0]), .b(7'b0110111), .eq(comparator_13_eq));  // open: gt, lt
  and and_3 (and_3_out[31], comparator_3_eq, comparator_5_eq);
  and and_4 (and_4_out[31], comparator_5_eq, comparator_6_eq);
  and and_5 (and_5_out[31], comparator_1_eq, comparator_2_eq);
  and and_6 (and_6_out[31], comparator_7_eq, comparator_8_eq);
  and and_7 (and_7_out[31], comparator_9_eq, comparator_10_eq);
  and and_8 (and_8_out[31], comparator_4_eq, comparator_5_eq);
  assign and_9_out = {32{and_10_out[31]}} & ram_1_dout;  // AND_Gate and_9, 32 bits wide
  and and_10 (and_10_out[31], comparator_11_eq, comparator_12_eq);
  and and_11 (and_11_out[31], EN, comparator_13_eq);
  and and_12 (and_12_out, EN, and_4_out[31]);
  assign and_13_out = {32{and_8_out[31]}} & {adder_2_out_2, adder_2_out[0]};  // AND_Gate and_13, 32 bits wide
  assign and_14_out = bit_extender_3_out & {32{and_6_out[31]}};  // AND_Gate and_14, 32 bits wide
  and and_15 (and_15_out, and_3_out[31], EN);
  and and_16 (and_16_out, EN, and_8_out[31]);
  assign and_17_out = {32{and_4_out[31]}} & adder_3_out;  // AND_Gate and_17, 32 bits wide
  or or_3 (or_3_out, and_6_out[31], and_15_out, and_12_out, and_10_out[31], and_11_out[31], and_16_out);
  GPR_RAM_32_32bit gpr_ram_32_32bit_1 (
    .R1addr0(rom_1_data[20]), .R1addr1(rom_1_data[21]), .R1addr2(rom_1_data[22]), .R1addr3(rom_1_data[23]),
    .R1addr4(rom_1_data[24]), .EN(or_3_out), .clk(clock_1_out), .Rst(Rst), .R2addr0(rom_1_data[15]),
    .R2addr1(rom_1_data[16]), .R2addr2(rom_1_data[17]), .R2addr3(rom_1_data[18]), .R2addr4(rom_1_data[19]),
    .Wdata(or_2_out), .Waddr0(rom_1_data[7]), .Waddr1(rom_1_data[8]), .Waddr2(rom_1_data[9]),
    .Waddr3(rom_1_data[10]), .Waddr4(rom_1_data[11]), .Read1(gpr_ram_32_32bit_1_read1),
    .Read2(gpr_ram_32_32bit_1_read2));
  Adder #(.width(32)) adder_2 (
    .a(gpr_ram_32_32bit_1_read2), .b(bit_extender_1_out), .out({adder_2_out_2, adder_2_out[0]}));  // open: cin, cout
  assign or_4_out = {32{and_6_out[31]}} | gpr_ram_32_32bit_1_read2;  // OR_Gate or_4, 32 bits wide
  Adder #(.width(32)) adder_3 (
    .a(gpr_ram_32_32bit_1_read1), .b(gpr_ram_32_32bit_1_read2), .out(adder_3_out));  // open: cin, cout
  assign and_18_out = or_4_out & {adder_2_out_2, adder_2_out[0]};  // AND_Gate and_18, 32 bits wide
  assign bit_extender_2_out = {{20{rom_1_data[31]}}, {rom_1_data[31:25], rom_1_data[11:7]}};  // Bit_Extender bit_extender_2
  assign or_5_out = {32{and_5_out[31]}} | {32{and_7_out[31]}};  // OR_Gate or_5, 32 bits wide
  Adder #(.width(32)) adder_4 (
    .a(gpr_ram_32_32bit_1_read2), .b(bit_extender_2_out), .out(adder_4_out));  // open: cin, cout
  assign and_19_out = or_5_out & adder_4_out;  // AND_Gate and_19, 32 bits wide
  assign and_20_out = {32{and_7_out[31]}} & gpr_ram_32_32bit_1_read1;  // AND_Gate and_20, 32 bits wide
  assign and_21_out = {32{and_5_out[31]}} & {gpr_ram_32_32bit_1_read1[7:0], gpr_ram_32_32bit_1_read1[7:0], gpr_ram_32_32bit_1_read1[7:0], gpr_ram_32_32bit_1_read1[7:0]};  // AND_Gate and_21, 32 bits wide
  assign or_6_out = and_20_out | and_21_out;  // OR_Gate or_6, 32 bits wide
  Decoder #(.select(2)) decoder_1 (
    .out0(decoder_1_out3[3]), .out1(decoder_1_out3[2]), .out2(decoder_1_out3[1]), .out3(decoder_1_out3[0]),
    .sel(and_19_out[1:0]), .en(1'b1));
  assign or_7_out = and_18_out[25:2] | and_19_out[25:2];  // OR_Gate or_7, 24 bits wide
  assign and_22_out = decoder_1_out3 & {4{and_5_out[31]}};  // AND_Gate and_22, 4 bits wide
  assign or_8_out = {4{and_7_out[31]}} | and_22_out;  // OR_Gate or_8, 4 bits wide
  or or_9 (or_9_out, and_5_out[31], and_7_out[31]);
  RAM #(.addrWidth(24), .asyncread("true"), .byteenables("byteEnables"), .dataWidth(32), .\type ("nonvolatile")) ram_1 (
    .addr(or_7_out), .we(or_9_out), .oe(1'b1), .clk(clock_1_out), .din(or_6_out), .dout(ram_1_dout),
    .be3(or_8_out[0]), .be2(or_8_out[1]), .be1(or_8_out[2]), .be0(or_8_out[3]));
  Multiplexer #(.select(2), .width(8)) multiplexer_1 (
    .in0(ram_1_dout[7:0]), .in1(ram_1_dout[15:8]), .in2(ram_1_dout[23:16]), .in3(ram_1_dout[31:24]),
    .out(multiplexer_1_out), .sel(and_18_out[1:0]));
  assign bit_extender_3_out = {{24{1'b0}}, multiplexer_1_out};  // Bit_Extender bit_extender_3

  // Notes on the sheet:
  //   contents of rom_1 (hex, n*v repeats v):
  //   413 52137 10113 10b7 22408093 80e7 fea12823 fe812e23 1437 40840413 ff014183 3401b3 1c183 ff114203
  //   440233 24203 4181b3 ff214203 440233 24203 4181b3 ff314203 440233 24203 4181b3 1237 40020213 320233
  //   24203 ffc12403 420233 420233 410233 a000193 fe312823 9c00193 fe312623 fec22203 20067 8067 ff410113
  //   100513 112423 10b7 21808093 80e7 fec10113 912423 494b7 6b048493 812623 112823 496b7 69068693 48413
  //   48713 fe012823 174183 fe3109a3 ff012183 fe812e23 fe312823 3d437 60040413 ff214203 420233 420233
  //   440233 22203 fe412623 ff114203 420233 420233 440233 22203 fe412423 ff014203 420233 420233 440233
  //   22203 fe412223 fed14183 fea14203 4181b3 fe714203 4181b3 fe312223 fee14183 feb14203 4181b3 fe3102a3
  //   fef14183 fe310323 fe412183 8237 20213 440433 ff314203 420233 420233 440233 22203 ffc12403 4181b3
  //   74503 350533 6a603 270713 468693 fe312a23 fec12423 31237 50020213 feb14183 4181b3 1c183 fe3103a3
  //   fea14183 4181b3 1c183 fe310323 fe914183 4181b3 1c183 fe3102a3 fe814183 4181b3 1c183 fe310223
  //   ff412183 fe412203 450533 150513 fea12823 fe812e23 1437 40840413 ff014183 3401b3 1c183 ff114203
  //   440233 24203 4181b3 ff214203 440233 24203 4181b3 ff314203 440233 24203 4181b3 1237 40020213 320233
  //   24503 ffc12403 e12223 d12023 1800093 80e7 412703 497b7 6c078793 12683 fee12823 fef12623 fe812e23
  //   fe912c23 1437 30040413 ff014183 340233 100193 320023 fec14183 3401b3 18023 24183 ff114483 940233
  //   100493 920023 fed14483 9404b3 48023 24483 9181b3 ff214483 940233 100493 920023 fee14483 9404b3 48023
  //   24483 9181b3 ff314483 940233 100493 920023 fef14483 9404b3 48023 24483 9181b3 1237 40020213 320233
  //   24203 ff812483 ffc12403 420233 420233 410233 37800193 fe312823 e000193 fe312623 fec22203 20067 49737
  //   67070713 72683 fe012823 14c203 fe4108a3 ff012203 4c503 450533 470713 e12023 fe312a23 fed12423 31237
  //   50020213 feb14183 4181b3 1c183 fe3103a3 fea14183 4181b3 1c183 fe310323 fe914183 4181b3 1c183
  //   fe3102a3 fe814183 4181b3 1c183 fe310223 ff412183 fe412203 450533 150513 fea12823 fe812e23 1437
  //   40840413 ff014183 3401b3 1c183 ff114203 440233 24203 4181b3 ff214203 440233 24203 4181b3 ff314203
  //   440233 24203 4181b3 1237 40020213 320233 24503 ffc12403 1800093 80e7 248493 497b7 6c078793 12703
  //   fe912823 fef12623 fe812e23 fe912c23 1437 30040413 ff014183 340233 100193 320023 fec14183 3401b3
  //   18023 24183 ff114483 940233 100493 920023 fed14483 9404b3 48023 24483 9181b3 ff214483 940233 100493
  //   920023 fee14483 9404b3 48023 24483 9181b3 ff314483 940233 100493 920023 fef14483 9404b3 48023 24483
  //   9181b3 1237 40020213 320233 24203 ff812483 ffc12403 420233 420233 410233 55c00193 fe312823 38000193
  //   fe312623 fec22203 20067 244683 144603 344703 444783 494b7 64048493 8*d686b3 fed12823 fec12623 116b7
  //   60068693 fe012223 ff314203 fe4102a3 fef14203 fe410223 fe412203 468233 24203 fe4105a3 ff214203
  //   fe4102a3 fee14203 fe410223 fe412203 468233 24203 fe410523 ff114203 fe4102a3 fed14203 fe410223
  //   fe412203 468233 24203 fe4104a3 ff014203 fe4102a3 fec14203 fe410223 fe412203 468233 24203 fe410423
  //   fe812683 4a503 fe012823 fee10923 fee12423 fe914203 fe4109a3 ff012703 fee12823 fed12623 11737
  //   60070713 fe012223 ff314203 fe4102a3 fef14203 fe410223 fe412203 470233 24203 fe4105a3 ff214203
  //   fe4102a3 fee14203 fe410223 fe412203 470233 24203 fe410523 ff114203 fe4102a3 fed14203 fe410223
  //   fe412203 470233 24203 fe4104a3 ff014203 fe4102a3 fec14203 fe410223 fe412203 470233 24203 fe410423
  //   fe812703 fe012823 fef109a3 ff012783 fef12823 fee12623 117b7 60078793 fe012223 ff314203 fe4102a3
  //   fef14203 fe410223 fe412203 478233 24203 fe4105a3 ff214203 fe4102a3 fee14203 fe410223 fe412203 478233
  //   24203 fe410523 ff114203 fe4102a3 fed14203 fe410223 fe412203 478233 24203 fe4104a3 ff014203 fe4102a3
  //   fec14203 fe410223 fe412203 478233 24203 fe410423 fe812783 fe312a23 fef12423 31237 50020213 feb14183
  //   4181b3 1c183 fe3103a3 fea14183 4181b3 1c183 fe310323 fe914183 4181b3 1c183 fe3102a3 fe814183 4181b3
  //   1c183 fe310223 ff412183 fe412203 450533 150513 fea12823 fe812e23 1437 40840413 ff014183 3401b3 1c183
  //   ff114203 440233 24203 4181b3 ff214203 440233 24203 4181b3 ff314203 440233 24203 4181b3 1237 400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
  //   Written datas of JALR
  //   Written datas of LUI
  //   SB
  //   LBU
  //   SW
  //   LUI
  //   JALR
  //   ADDI
  //   ADD
  //   decide datas which wil be written
  //   LW
  //   Written datas of ADDI
  //   Written datas of LW
  //   Written datas of LBU
  //   Written datas of ADD
endmodule

module PC_Register_32_bit (
  input  [31:0] addr,
  input  flag,
  input  EN,
  input  clk,
  input  Rst,
  output Out1,
  output Out2,
  output Out3,
  output Out4,
  output out_10,
  output out_11,
  output out_12,
  output out_13,
  output out_14,
  output out_15,
  output out_16,
  output out_17,
  output out_18,
  output out_19,
  output out_20,
  output out_21,
  output out_22,
  output out_23,
  output out_24,
  output out_25,
  output out_26,
  output out_27,
  output out_28,
  output out_29,
  output out_30,
  output out_31,
  output out_32,
  output out_33,
  output Out28,
  output Out29,
  output Out30,
  output Out31,
  output [31:0] Out_32_bit
);

  wire [31:0] adder_1_out, and_1_out, and_2_out, or_1_out;
  wire [31:31] not_1_out;

  not not_1 (not_1_out[31], flag);
  assign and_1_out = addr & {32{not_1_out[31]}};  // AND_Gate and_1, 32 bits wide
  assign or_1_out = and_1_out | and_2_out;  // OR_Gate or_1, 32 bits wide
  Register #(.width(32)) register_1 (
    .D(or_1_out), .en(EN), .clk(clk),
    .Q({Out31, Out30, Out29, Out28, Out_32_bit[27], out_32, out_31, out_30, out_29, out_28, out_27, out_26, out_25, out_24, out_23, out_22, out_21, out_20, out_19, out_18, out_17, out_16, out_15, out_14, out_13, out_12, out_11, out_10, Out4, Out3, Out2, Out1}),
    .clr(Rst));
  assign and_2_out = {32{flag}} & adder_1_out;  // AND_Gate and_2, 32 bits wide
  Adder #(.width(32)) adder_1 (
    .a(32'h4),
    .b({Out31, Out30, Out29, Out28, Out_32_bit[27], out_32, out_31, out_30, out_29, out_28, out_27, out_26, out_25, out_24, out_23, out_22, out_21, out_20, out_19, out_18, out_17, out_16, out_15, out_14, out_13, out_12, out_11, out_10, Out4, Out3, Out2, Out1}),
    .out(adder_1_out));  // open: cin, cout

  assign {Out_32_bit[31:28], Out_32_bit[26:0]} = {Out31, Out30, Out29, Out28, out_32, out_31, out_30, out_29, out_28, out_27, out_26, out_25, out_24, out_23, out_22, out_21, out_20, out_19, out_18, out_17, out_16, out_15, out_14, out_13, out_12, out_11, out_10, Out4, Out3, Out2, Out1};
  assign out_33 = Out_32_bit[27];
endmodule

module ROM_32_bit (
  input  In_0,
  input  In_1,
  input  In_2,
  input  In_3,
  input  In_4,
  output Out0,
  output out_7,
  output out_8,
  output out_9,
  output out_10,
  output out_11,
  output out_12,
  output Out7,
  output out_14,
  output out_15,
  output out_16,
  output out_17,
  output out_18,
  output out_19,
  output out_20,
  output Out15,
  output out_22,
  output out_23,
  output out_24,
  output out_25,
  output out_26,
  output out_27,
  output out_28,
  output Out23,
  output out_30,
  output out_31,
  output out_32,
  output out_33,
  output out_34,
  output out_35,
  output out_36,
  output Out31
);

  Multiplexer #(.select(5), .width(32)) multiplexer_1 (
    .in0(32'h11137), .in1(32'h7800193), .in2(32'h312023), .in3(32'h12203), .in4(32'h4182b3),
    .in5(32'h5101a3), .in6(32'h314303), .in7(32'h14303),
    .out({Out31, out_36, out_35, out_34, out_33, out_32, out_31, out_30, Out23, out_28, out_27, out_26, out_25, out_24, out_23, out_22, Out15, out_20, out_19, out_18, out_17, out_16, out_15, out_14, Out7, out_12, out_11, out_10, out_9, out_8, out_7, Out0}),
    .sel({In_4, In_3, In_2, In_1, In_0}));  // open: in8, in9, in10, in11, in12, in13, in14, in15, in16, in17, in18, in19, in20, in21, in22, in23, in24, in25, in26, in27, in28, in29, in30, in31
endmodule

module GPR_RAM_32_32bit (
  input  R1addr0,
  input  R1addr1,
  input  R1addr2,
  input  R1addr3,
  input  R1addr4,
  input  EN,
  input  clk,
  input  Rst,
  input  R2addr0,
  input  R2addr1,
  input  R2addr2,
  input  R2addr3,
  input  R2addr4,
  input  [31:0] Wdata,
  input  Waddr0,
  input  Waddr1,
  input  Waddr2,
  input  Waddr3,
  input  Waddr4,
  output [31:0] Read1,
  output [31:0] Read2
);

  wire demultiplexer_2_out1, demultiplexer_2_out2, demultiplexer_2_out3, demultiplexer_2_out4,
       demultiplexer_2_out5, demultiplexer_2_out6, demultiplexer_2_out7, demultiplexer_2_out8,
       demultiplexer_2_out9, demultiplexer_2_out10, demultiplexer_2_out11, demultiplexer_2_out12,
       demultiplexer_2_out13, demultiplexer_2_out14, demultiplexer_2_out15, demultiplexer_2_out16,
       demultiplexer_2_out17, demultiplexer_2_out18, demultiplexer_2_out19, demultiplexer_2_out20,
       demultiplexer_2_out21, demultiplexer_2_out22, demultiplexer_2_out23, demultiplexer_2_out24,
       demultiplexer_2_out25, demultiplexer_2_out26, demultiplexer_2_out27, demultiplexer_2_out28,
       demultiplexer_2_out29, demultiplexer_2_out30, demultiplexer_2_out31;
  wire [31:0] demultiplexer_1_out1, demultiplexer_1_out2, demultiplexer_1_out3, demultiplexer_1_out4,
       demultiplexer_1_out5, demultiplexer_1_out6, demultiplexer_1_out7, demultiplexer_1_out8,
       demultiplexer_1_out9, demultiplexer_1_out10, demultiplexer_1_out11, demultiplexer_1_out12,
       demultiplexer_1_out13, demultiplexer_1_out14, demultiplexer_1_out15, demultiplexer_1_out16,
       demultiplexer_1_out17, demultiplexer_1_out18, demultiplexer_1_out19, demultiplexer_1_out20,
       demultiplexer_1_out21, demultiplexer_1_out22, demultiplexer_1_out23, demultiplexer_1_out24,
       demultiplexer_1_out25, demultiplexer_1_out26, demultiplexer_1_out27, demultiplexer_1_out28,
       demultiplexer_1_out29, demultiplexer_1_out30, demultiplexer_1_out31, register_1_q, register_2_q,
       register_3_q, register_4_q, register_5_q, register_6_q, register_7_q, register_8_q, register_9_q,
       register_10_q, register_11_q, register_12_q, register_13_q, register_14_q, register_15_q,
       register_16_q, register_17_q, register_18_q, register_19_q, register_20_q, register_21_q,
       register_22_q, register_23_q, register_24_q, register_25_q, register_26_q, register_27_q,
       register_28_q, register_29_q, register_30_q, register_31_q, register_32_q;

  Demultiplexer #(.select(5), .width(32)) demultiplexer_1 (
    .out1(demultiplexer_1_out1), .out2(demultiplexer_1_out2), .out3(demultiplexer_1_out3),
    .out4(demultiplexer_1_out4), .out5(demultiplexer_1_out5), .out6(demultiplexer_1_out6),
    .out7(demultiplexer_1_out7), .out8(demultiplexer_1_out8), .out9(demultiplexer_1_out9),
    .out10(demultiplexer_1_out10), .out11(demultiplexer_1_out11), .out12(demultiplexer_1_out12),
    .out13(demultiplexer_1_out13), .out14(demultiplexer_1_out14), .out15(demultiplexer_1_out15),
    .out16(demultiplexer_1_out16), .out17(demultiplexer_1_out17), .out18(demultiplexer_1_out18),
    .out19(demultiplexer_1_out19), .out20(demultiplexer_1_out20), .out21(demultiplexer_1_out21),
    .out22(demultiplexer_1_out22), .out23(demultiplexer_1_out23), .out24(demultiplexer_1_out24),
    .out25(demultiplexer_1_out25), .out26(demultiplexer_1_out26), .out27(demultiplexer_1_out27),
    .out28(demultiplexer_1_out28), .out29(demultiplexer_1_out29), .out30(demultiplexer_1_out30),
    .out31(demultiplexer_1_out31), .in(Wdata), .sel({Waddr4, Waddr3, Waddr2, Waddr1, Waddr0}));  // open: out0
  Register #(.width(32)) register_1 (.D({32{1'b0}}), .clk(clk), .Q(register_1_q), .clr(Rst));  // open: en
  Register #(.width(32)) register_2 (
    .D(demultiplexer_1_out1), .en(demultiplexer_2_out1), .clk(clk), .Q(register_2_q), .clr(Rst));
  Register #(.width(32)) register_3 (
    .D(demultiplexer_1_out2), .en(demultiplexer_2_out2), .clk(clk), .Q(register_3_q), .clr(Rst));
  Register #(.width(32)) register_4 (
    .D(demultiplexer_1_out3), .en(demultiplexer_2_out3), .clk(clk), .Q(register_4_q), .clr(Rst));
  Register #(.width(32)) register_5 (
    .D(demultiplexer_1_out16), .en(demultiplexer_2_out16), .clk(clk), .Q(register_5_q), .clr(Rst));
  Register #(.width(32)) register_6 (
    .D(demultiplexer_1_out17), .en(demultiplexer_2_out17), .clk(clk), .Q(register_6_q), .clr(Rst));
  Register #(.width(32)) register_7 (
    .D(demultiplexer_1_out18), .en(demultiplexer_2_out18), .clk(clk), .Q(register_7_q), .clr(Rst));
  Register #(.width(32)) register_8 (
    .D(demultiplexer_1_out19), .en(demultiplexer_2_out19), .clk(clk), .Q(register_8_q), .clr(Rst));
  Demultiplexer #(.select(5)) demultiplexer_2 (
    .out1(demultiplexer_2_out1), .out2(demultiplexer_2_out2), .out3(demultiplexer_2_out3),
    .out4(demultiplexer_2_out4), .out5(demultiplexer_2_out5), .out6(demultiplexer_2_out6),
    .out7(demultiplexer_2_out7), .out8(demultiplexer_2_out8), .out9(demultiplexer_2_out9),
    .out10(demultiplexer_2_out10), .out11(demultiplexer_2_out11), .out12(demultiplexer_2_out12),
    .out13(demultiplexer_2_out13), .out14(demultiplexer_2_out14), .out15(demultiplexer_2_out15),
    .out16(demultiplexer_2_out16), .out17(demultiplexer_2_out17), .out18(demultiplexer_2_out18),
    .out19(demultiplexer_2_out19), .out20(demultiplexer_2_out20), .out21(demultiplexer_2_out21),
    .out22(demultiplexer_2_out22), .out23(demultiplexer_2_out23), .out24(demultiplexer_2_out24),
    .out25(demultiplexer_2_out25), .out26(demultiplexer_2_out26), .out27(demultiplexer_2_out27),
    .out28(demultiplexer_2_out28), .out29(demultiplexer_2_out29), .out30(demultiplexer_2_out30),
    .out31(demultiplexer_2_out31), .in(EN), .sel({Waddr4, Waddr3, Waddr2, Waddr1, Waddr0}));  // open: out0
  Register #(.width(32)) register_9 (
    .D(demultiplexer_1_out4), .en(demultiplexer_2_out4), .clk(clk), .Q(register_9_q), .clr(Rst));
  Register #(.width(32)) register_10 (
    .D(demultiplexer_1_out5), .en(demultiplexer_2_out5), .clk(clk), .Q(register_10_q), .clr(Rst));
  Register #(.width(32)) register_11 (
    .D(demultiplexer_1_out6), .en(demultiplexer_2_out6), .clk(clk), .Q(register_11_q), .clr(Rst));
  Register #(.width(32)) register_12 (
    .D(demultiplexer_1_out7), .en(demultiplexer_2_out7), .clk(clk), .Q(register_12_q), .clr(Rst));
  Register #(.width(32)) register_13 (
    .D(demultiplexer_1_out20), .en(demultiplexer_2_out20), .clk(clk), .Q(register_13_q), .clr(Rst));
  Register #(.width(32)) register_14 (
    .D(demultiplexer_1_out21), .en(demultiplexer_2_out21), .clk(clk), .Q(register_14_q), .clr(Rst));
  Register #(.width(32)) register_15 (
    .D(demultiplexer_1_out22), .en(demultiplexer_2_out22), .clk(clk), .Q(register_15_q), .clr(Rst));
  Register #(.width(32)) register_16 (
    .D(demultiplexer_1_out23), .en(demultiplexer_2_out23), .clk(clk), .Q(register_16_q), .clr(Rst));
  Register #(.width(32)) register_17 (
    .D(demultiplexer_1_out8), .en(demultiplexer_2_out8), .clk(clk), .Q(register_17_q), .clr(Rst));
  Register #(.width(32)) register_18 (
    .D(demultiplexer_1_out9), .en(demultiplexer_2_out9), .clk(clk), .Q(register_18_q), .clr(Rst));
  Register #(.width(32)) register_19 (
    .D(demultiplexer_1_out10), .en(demultiplexer_2_out10), .clk(clk), .Q(register_19_q), .clr(Rst));
  Register #(.width(32)) register_20 (
    .D(demultiplexer_1_out11), .en(demultiplexer_2_out11), .clk(clk), .Q(register_20_q), .clr(Rst));
  Register #(.width(32)) register_21 (
    .D(demultiplexer_1_out24), .en(demultiplexer_2_out24), .clk(clk), .Q(register_21_q), .clr(Rst));
  Register #(.width(32)) register_22 (
    .D(demultiplexer_1_out25), .en(demultiplexer_2_out25), .clk(clk), .Q(register_22_q), .clr(Rst));
  Register #(.width(32)) register_23 (
    .D(demultiplexer_1_out26), .en(demultiplexer_2_out26), .clk(clk), .Q(register_23_q), .clr(Rst));
  Register #(.width(32)) register_24 (
    .D(demultiplexer_1_out27), .en(demultiplexer_2_out27), .clk(clk), .Q(register_24_q), .clr(Rst));
  Register #(.width(32)) register_25 (
    .D(demultiplexer_1_out12), .en(demultiplexer_2_out12), .clk(clk), .Q(register_25_q), .clr(Rst));
  Register #(.width(32)) register_26 (
    .D(demultiplexer_1_out13), .en(demultiplexer_2_out13), .clk(clk), .Q(register_26_q), .clr(Rst));
  Register #(.width(32)) register_27 (
    .D(demultiplexer_1_out14), .en(demultiplexer_2_out14), .clk(clk), .Q(register_27_q), .clr(Rst));
  Register #(.width(32)) register_28 (
    .D(demultiplexer_1_out15), .en(demultiplexer_2_out15), .clk(clk), .Q(register_28_q), .clr(Rst));
  Register #(.width(32)) register_29 (
    .D(demultiplexer_1_out28), .en(demultiplexer_2_out28), .clk(clk), .Q(register_29_q), .clr(Rst));
  Register #(.width(32)) register_30 (
    .D(demultiplexer_1_out29), .en(demultiplexer_2_out29), .clk(clk), .Q(register_30_q), .clr(Rst));
  Register #(.width(32)) register_31 (
    .D(demultiplexer_1_out30), .en(demultiplexer_2_out30), .clk(clk), .Q(register_31_q), .clr(Rst));
  Register #(.width(32)) register_32 (
    .D(demultiplexer_1_out31), .en(demultiplexer_2_out31), .clk(clk), .Q(register_32_q), .clr(Rst));
  Multiplexer #(.select(5), .width(32)) multiplexer_1 (
    .in0(register_1_q), .in1(register_2_q), .in2(register_3_q), .in3(register_4_q), .in4(register_9_q),
    .in5(register_10_q), .in6(register_11_q), .in7(register_12_q), .in8(register_17_q), .in9(register_18_q),
    .in10(register_19_q), .in11(register_20_q), .in12(register_25_q), .in13(register_26_q),
    .in14(register_27_q), .in15(register_28_q), .in16(register_5_q), .in17(register_6_q),
    .in18(register_7_q), .in19(register_8_q), .in20(register_13_q), .in21(register_14_q),
    .in22(register_15_q), .in23(register_16_q), .in24(register_21_q), .in25(register_22_q),
    .in26(register_23_q), .in27(register_24_q), .in28(register_29_q), .in29(register_30_q),
    .in30(register_31_q), .in31(register_32_q), .out(Read1),
    .sel({R1addr4, R1addr3, R1addr2, R1addr1, R1addr0}));
  Multiplexer #(.select(5), .width(32)) multiplexer_2 (
    .in0(register_1_q), .in1(register_2_q), .in2(register_3_q), .in3(register_4_q), .in4(register_9_q),
    .in5(register_10_q), .in6(register_11_q), .in7(register_12_q), .in8(register_17_q), .in9(register_18_q),
    .in10(register_19_q), .in11(register_20_q), .in12(register_25_q), .in13(register_26_q),
    .in14(register_27_q), .in15(register_28_q), .in16(register_5_q), .in17(register_6_q),
    .in18(register_7_q), .in19(register_8_q), .in20(register_13_q), .in21(register_14_q),
    .in22(register_15_q), .in23(register_16_q), .in24(register_21_q), .in25(register_22_q),
    .in26(register_23_q), .in27(register_24_q), .in28(register_29_q), .in29(register_30_q),
    .in30(register_31_q), .in31(register_32_q), .out(Read2),
    .sel({R2addr4, R2addr3, R2addr2, R2addr1, R2addr0}));

  // Notes on the sheet:
  //   Wdata: initial=0x80000000
  //   Write
  //   Read1
  //   Read2
endmodule

module temp (
  input  addr0,
  input  addr1,
  input  addr2,
  input  addr3,
  input  in_5,
  input  in_6,
  input  in_7,
  input  in_8,
  input  in_9,
  input  in_10,
  input  in_11,
  input  in_12,
  input  in_13,
  input  in_14,
  input  in_15,
  input  in_16,
  input  in_17,
  input  in_18,
  input  in_19,
  input  in_20,
  input  in_21,
  input  in_22,
  input  in_23,
  input  in_24,
  input  in_25,
  input  in_26,
  input  in_27,
  input  in_28,
  input  addr28,
  input  addr29,
  input  addr30,
  input  addr31
);
endmodule

module RAM_of_memory (
);

  RAM #(.addrWidth(16), .asyncread("true"), .byteenables("byteEnables"), .dataWidth(32), .\type ("nonvolatile")) ram_1 ();  // open: addr, we, oe, clk, din, dout, be3, be2, be1, be0
endmodule

module Sixteen_bit_counter (
  input  EN,
  input  clk,
  input  Rst,
  output [15:0] out_4
);

  wire [15:0] adder_1_out;

  Register #(.width(16)) register_1 (.D(adder_1_out), .en(EN), .clk(clk), .Q(out_4), .clr(Rst));
  Adder #(.width(16)) adder_1 (.a(out_4), .b(16'h1), .out(adder_1_out));  // open: cin, cout
endmodule
